// Logisim project 5bitcounter (1) (1).circ as structural Verilog: 1 circuit, main circuit main
module main (
  input  UpOrDown,
  input  Clock,
  input  in_3,
  output out_4,
  output out_5,
  output out_6,
  output out_7,
  output out_8
);

  wire and_1_out, and_2_out, and_3_out, and_4_out, and_5_out, and_6_out, and_7_out, and_8_out, d_ff_1_qn,
       d_ff_2_qn, d_ff_3_qn, d_ff_4_qn, not_1_out, or_1_out, or_2_out, or_3_out, or_4_out, or_5_out,
       xor_1_out, xor_2_out, xor_3_out, xor_4_out, xor_5_out;

  not not_1 (not_1_out, UpOrDown);
  and and_1 (and_1_out, not_1_out, d_ff_1_qn);
  and and_2 (and_2_out, and_1_out, d_ff_2_qn);
  and and_3 (and_3_out, and_2_out, d_ff_3_qn);
  and and_4 (and_4_out, and_3_out, d_ff_4_qn);
  and and_5 (and_5_out, UpOrDown, out_4);
  and and_6 (and_6_out, and_5_out, out_5);
  and and_7 (and_7_out, and_6_out, out_6);
  and and_8 (and_8_out, and_7_out, out_7);
  or or_1 (or_1_out, UpOrDown, not_1_out);
  or or_2 (or_2_out, and_5_out, and_1_out);
  or or_3 (or_3_out, and_6_out, and_2_out);
  or or_4 (or_4_out, and_7_out, and_3_out);
  or or_5 (or_5_out, and_8_out, and_4_out);
  xor xor_1 (xor_1_out, out_4, or_1_out);
  xor xor_2 (xor_2_out, out_6, or_3_out);
  xor xor_3 (xor_3_out, out_7, or_4_out);
  xor xor_4 (xor_4_out, out_8, or_5_out);
  xor xor_5 (xor_5_out, out_5, or_2_out);
  D_Flip_Flop d_ff_1 (.clk(Clock), .D(xor_1_out), .Q(out_4), .Qn(d_ff_1_qn), .reset(in_3));  // open: preset, en
  D_Flip_Flop d_ff_2 (.clk(Clock), .D(xor_5_out), .Q(out_5), .Qn(d_ff_2_qn), .reset(in_3));  // open: preset, en
  D_Flip_Flop d_ff_3 (.clk(Clock), .D(xor_2_out), .Q(out_6), .Qn(d_ff_3_qn), .reset(in_3));  // open: preset, en
  D_Flip_Flop d_ff_4 (.clk(Clock), .D(xor_3_out), .Q(out_7), .Qn(d_ff_4_qn), .reset(in_3));  // open: preset, en
  D_Flip_Flop d_ff_5 (.clk(Clock), .D(xor_4_out), .Q(out_8), .reset(in_3));  // open: Qn, preset, en
endmodule
