// Logisim project idverifier.circ as structural Verilog: 1 circuit, main circuit main
module main (
  input  in_1,
  input  in_2,
  input  in_3,
  input  in_4,
  input  in_5,
  input  in_6,
  input  in_7,
  input  in_8,
  output out_9
);

  wire and_1_out, and_2_out, and_3_out, xnor_1_out, xnor_2_out, xnor_3_out, xnor_4_out, xnor_5_out,
       xnor_6_out, xnor_7_out, xnor_8_out, xnor_9_out, xnor_10_out, xnor_11_out, xnor_12_out, xnor_13_out,
       xnor_14_out, xnor_15_out, xnor_16_out, xnor_17_out, xnor_18_out, xnor_19_out, xnor_20_out,
       xnor_21_out, xnor_22_out, xnor_23_out, xnor_24_out;

  xnor xnor_1 (xnor_1_out, in_1, 1'b1);
  xnor xnor_2 (xnor_2_out, in_2, 1'b1);
  xnor xnor_3 (xnor_3_out, in_3, 1'b1);
  xnor xnor_4 (xnor_4_out, in_4, 1'b1);
  xnor xnor_5 (xnor_5_out, in_5, 1'b1);
  xnor xnor_6 (xnor_6_out, in_6, 1'b1);
  xnor xnor_7 (xnor_7_out, in_7, 1'b1);
  xnor xnor_8 (xnor_8_out, in_8, 1'b1);
  xnor xnor_9 (xnor_9_out, in_1, 1'b0);
  xnor xnor_10 (xnor_10_out, in_2, 1'b0);
  xnor xnor_11 (xnor_11_out, in_3, 1'b0);
  xnor xnor_12 (xnor_12_out, in_4, 1'b1);
  xnor xnor_13 (xnor_13_out, in_5, 1'b1);
  xnor xnor_14 (xnor_14_out, in_6, 1'b1);
  xnor xnor_15 (xnor_15_out, in_7, 1'b1);
  xnor xnor_16 (xnor_16_out, in_8, 1'b1);
  xnor xnor_17 (xnor_17_out, in_1, 1'b0);
  xnor xnor_18 (xnor_18_out, in_2, 1'b0);
  xnor xnor_19 (xnor_19_out, in_3, 1'b0);
  xnor xnor_20 (xnor_20_out, in_4, 1'b0);
  xnor xnor_21 (xnor_21_out, in_5, 1'b0);
  xnor xnor_22 (xnor_22_out, in_6, 1'b0);
  xnor xnor_23 (xnor_23_out, in_7, 1'b0);
  xnor xnor_24 (xnor_24_out, in_8, 1'b1);
  and and_1 (and_1_out, xnor_9_out, xnor_10_out, xnor_11_out, xnor_12_out, xnor_13_out, xnor_14_out, xnor_15_out, xnor_16_out);
  and and_2 (and_2_out, xnor_17_out, xnor_18_out, xnor_19_out, xnor_20_out, xnor_21_out, xnor_22_out, xnor_23_out, xnor_24_out);
  and and_3 (and_3_out, xnor_1_out, xnor_2_out, xnor_3_out, xnor_4_out, xnor_5_out, xnor_6_out, xnor_7_out, xnor_8_out);
  or or_1 (out_9, and_1_out, and_2_out, and_3_out);
endmodule
