// Logisim project COMPARATOR (2).circ as structural Verilog: 1 circuit, main circuit main
module main (
  input  A0,
  input  B0,
  input  A1,
  input  B1,
  input  A2,
  input  B2,
  input  A3,
  input  B3,
  input  A4,
  input  B4,
  output out_11,
  output out_12,
  output out_13
);

  wire and_1_out, and_2_out, and_3_out, and_4_out, and_5_out, not_1_out, not_2_out, not_3_out, not_4_out,
       not_5_out, xnor_1_out, xnor_2_out, xnor_3_out, xnor_4_out, xnor_5_out;

  xnor xnor_1 (xnor_1_out, A0, B0);
  xnor xnor_2 (xnor_2_out, A1, B1);
  xnor xnor_3 (xnor_3_out, A2, B2);
  xnor xnor_4 (xnor_4_out, A3, B3);
  xnor xnor_5 (xnor_5_out, A4, B4);
  not not_1 (not_1_out, B0);
  not not_2 (not_2_out, B1);
  not not_3 (not_3_out, B2);
  not not_4 (not_4_out, B3);
  not not_5 (not_5_out, B4);
  and and_1 (and_1_out, not_1_out, A0, xnor_2_out, xnor_3_out, xnor_4_out, xnor_5_out);
  and and_2 (and_2_out, xnor_3_out, xnor_4_out, not_2_out, A1, xnor_5_out);
  and and_3 (and_3_out, not_3_out, A2, xnor_4_out, xnor_5_out);
  and and_4 (and_4_out, A3, not_4_out, xnor_5_out);
  and and_5 (and_5_out, not_5_out, A4);
  and and_6 (out_13, xnor_1_out, xnor_2_out, xnor_3_out, xnor_4_out, xnor_5_out);
  or or_1 (out_11, and_1_out, and_2_out, and_3_out, and_4_out, and_5_out);
  nor nor_1 (out_12, out_11, out_13);

  // Notes on the sheet:
  //   A>B
  //   A=B
endmodule
