// Logisim project subtractor (2).circ as structural Verilog: 1 circuit, main circuit main
module main (
  input  bin,
  input  b0,
  input  b1,
  input  b2,
  input  b3,
  input  b4,
  input  a0,
  input  a1,
  input  a2,
  input  a3,
  input  a4,
  output d0,
  output d1,
  output d2,
  output d3,
  output d4
);

  wire and_1_out, and_2_out, and_3_out, and_4_out, and_5_out, and_6_out, and_7_out, and_8_out, and_9_out,
       and_10_out, not_1_out, not_2_out, not_3_out, not_4_out, not_5_out, or_1_out, or_2_out, or_3_out,
       xor_1_out, xor_2_out, xor_3_out, xor_4_out, xor_5_out, xor_6_out, xor_7_out, xor_8_out, xor_9_out,
       xor_10_out, xor_16_out;

  not not_1 (not_1_out, a0);
  not not_2 (not_2_out, a1);
  not not_3 (not_3_out, a2);
  not not_4 (not_4_out, a3);
  not not_5 (not_5_out, a4);
  xor xor_1 (xor_1_out, bin, a0);
  xor xor_2 (xor_2_out, b0, bin);
  xor xor_3 (xor_3_out, or_1_out, a1);
  xor xor_4 (xor_4_out, b1, or_1_out);
  xor xor_5 (xor_5_out, xor_16_out, a2);
  xor xor_6 (xor_6_out, b2, xor_16_out);
  xor xor_7 (xor_7_out, or_2_out, a3);
  xor xor_8 (xor_8_out, b3, or_2_out);
  xor xor_9 (xor_9_out, or_3_out, a4);
  xor xor_10 (xor_10_out, b4, or_3_out);
  xor xor_11 (d0, b0, xor_1_out);
  and and_1 (and_1_out, not_1_out, xor_2_out);
  xor xor_12 (d1, b1, xor_3_out);
  and and_2 (and_2_out, not_2_out, xor_4_out);
  xor xor_13 (d2, b2, xor_5_out);
  xor xor_14 (d3, b3, xor_7_out);
  xor xor_15 (d4, b4, xor_9_out);
  and and_3 (and_3_out, bin, b0);
  and and_4 (and_4_out, or_1_out, b1);
  and and_5 (and_5_out, xor_16_out, b2);
  and and_6 (and_6_out, not_3_out, xor_6_out);
  and and_7 (and_7_out, or_2_out, b3);
  and and_8 (and_8_out, not_4_out, xor_8_out);
  and and_9 (and_9_out, or_3_out, b4);
  and and_10 (and_10_out, not_5_out, xor_10_out);
  or or_1 (or_1_out, and_3_out, and_1_out);
  xor xor_16 (xor_16_out, and_4_out, and_2_out);
  or or_2 (or_2_out, and_5_out, and_6_out);
  or or_3 (or_3_out, and_7_out, and_8_out);
  // OR_Gate or_4 has open pins: in0=and_9_out, in1=and_10_out, out=open
  LED led_1 (.in(d0));
endmodule
